// Logisim project 332_pipelined.circ as structural Verilog: 5 circuits, main circuit main
module main (
  input  [7:0] in_1,
  input  Reset,
  input  in_3,
  input  [1:0] in_4,
  output [3:0] mem_address,
  output [3:0] oppcode,
  output [1:0] rs,
  output [1:0] rt,
  output [1:0] rd,
  output R_f_flag,
  output I_f_flag,
  output [3:0] mem_address_2,
  output [1:0] write_reg,
  output [3:0] mem_address_3,
  output [9:0] RS_Data,
  output [9:0] RT_Data,
  output [9:0] RD_Data,
  output [9:0] ALU_out,
  output [9:0] mem_data
);

  wire Clk, I, lui, lw, or_1_out, R, sw, WR_flag;
  wire [1:0] alu_opp, IWrite;
  wire [3:0] bit_extender_2_out;
  wire [7:0] adder_1_out, PC_q;
  wire [9:0] exadd, IWRD;

  Clock Clock (.out(Clk));
  Register PC (.D(adder_1_out), .en(in_3), .Q(PC_q), .clk(Clk));  // open: clr
  Adder adder_1 (.a(PC_q), .b(in_1), .out(adder_1_out));  // open: cin, cout
  or or_1 (or_1_out, sw, lw);
  ROM #(.dataWidth(10)) rom_1 (.addr(PC_q), .data({oppcode, rs, mem_address_2}), .sel(in_3));
  RAM #(.addrWidth(4), .dataWidth(10), .bus("separate")) ram_1 (
    .addr(mem_address_3), .din(RT_Data), .data(mem_data), .str(sw), .sel(or_1_out), .clk(Clk), .ld(lw),
    .clr(Reset));
  control_unit control_unit_1 (
    .in_1(oppcode), .Format(R_f_flag), .LW(lw), .SW(sw), .LUI(lui), .ALU_Opp(alu_opp), .R(R), .I(I),
    .Write_Reg(WR_flag));
  Multiplexer #(.width(10)) multiplexer_1 (.in0(IWRD), .in1(ALU_out), .out(RD_Data), .sel(R_f_flag), .en(WR_flag));
  assign exadd = {{6{1'b0}}, mem_address_2};  // Bit_Extender bit_extender_1
  Multiplexer #(.width(2)) multiplexer_2 (.in0(rs), .in1(mem_address_2[3:2]), .out(IWrite), .sel(lw), .en(I));
  Multiplexer #(.width(10)) multiplexer_3 (.in0(mem_data), .in1(exadd), .out(IWRD), .sel(lui), .en(I));
  Multiplexer #(.width(2)) multiplexer_4 (
    .in0(IWrite), .in1(mem_address_2[1:0]), .out(write_reg), .sel(R_f_flag), .en(WR_flag));
  not not_1 (I_f_flag, R_f_flag);
  Register_FIle register_file_1 (
    .Write_Reg(write_reg), .Write_Data(RD_Data), .Ven_EN(WR_flag), .Clock(Clk),
    .Read_Data1({RS_Data[9:4], mem_address}), .Read_Reg1(rs), .Read_Data_2(RT_Data),
    .Read_Reg2(mem_address_2[3:2]), .reset(Reset));
  ALU alu_1 (
    .RS({RS_Data[9:4], mem_address}), .RT(RT_Data), .Select_Opperation(alu_opp), .OUTPUT(ALU_out));  // open: Cin, Cout
  assign bit_extender_2_out = {{2{1'b0}}, mem_address_2[1:0]};  // Bit_Extender bit_extender_2
  Adder #(.width(4)) adder_2 (.a(mem_address), .b(bit_extender_2_out), .out(mem_address_3));  // open: cin, cout

  assign rd = mem_address_2[1:0];
  assign RS_Data[3:0] = mem_address;
  assign rt = mem_address_2[3:2];

  // Other names for the same wires on the sheet: opp_C[3:0] = oppcode; Address[3:0] = mem_address_2; en = in_3;
  //   Fflg = R_f_flag; lwAdd[3:0] = mem_address_3; Res = Reset; add[3:0] = mem_address;
  //   RR1D[9:0] = {RS_Data[9:4], mem_address}; RR2D[9:0] = RT_Data; WR1[1:0] = write_reg; WRD[9:0] = RD_Data

  // Notes on the sheet:
  //   instruction mem
  //   1.oppcode, 2. rs, 3.rt, 4.rd
  //   Data mem
  //   lui/lw
endmodule

// REG FILE
module Register_FIle (
  input  [9:0] Write_Data,
  input  [1:0] Write_Reg,
  input  reset,
  input  Ven_EN,
  input  Clock,
  input  [1:0] Read_Reg1,
  input  [1:0] Read_Reg2,
  output [9:0] Read_Data1,
  output [9:0] Read_Data_2
);

  wire R1, R2, R3, R4;
  wire [9:0] Dout1, Dout2, Dout3, Dout4;

  Decoder #(.select(2)) decoder_1 (.out0(R1), .out1(R2), .out2(R3), .out3(R4), .sel(Write_Reg), .en(Ven_EN));
  Register #(.width(10)) u_R1 (.D(Write_Data), .en(R1), .Q(Dout1), .clk(Clock), .clr(reset));
  Register #(.width(10)) u_R3 (.D(Write_Data), .en(R3), .Q(Dout3), .clk(Clock), .clr(reset));
  Register #(.width(10)) u_R2 (.D(Write_Data), .en(R2), .Q(Dout2), .clk(Clock), .clr(reset));
  Register #(.width(10)) u_R4 (.D(Write_Data), .en(R4), .Q(Dout4), .clk(Clock), .clr(reset));
  Multiplexer #(.select(2), .width(10), .enable("false")) multiplexer_1 (
    .in0(Dout1), .in1(Dout2), .in2(Dout3), .in3(Dout4), .out(Read_Data1), .sel(Read_Reg1));
  Multiplexer #(.select(2), .width(10), .enable("false")) multiplexer_2 (
    .in0(Dout1), .in1(Dout2), .in2(Dout3), .in3(Dout4), .out(Read_Data_2), .sel(Read_Reg2));

  // Other names for the same wires on the sheet: clk = Clock; Din[9:0] = Write_Data; do1[9:0] = Read_Data1;
  //   do2[9:0] = Read_Data_2; en = Ven_EN; RD1[1:0] = Read_Reg1; RD2[1:0] = Read_Reg2; refresh = reset;
  //   writeReg[1:0] = Write_Reg
endmodule

module ALU (
  input  [1:0] Select_Opperation,
  input  Cin,
  input  [9:0] RS,
  input  [9:0] RT,
  output Cout,
  output [9:0] OUTPUT
);

  wire [9:0] Add, And, Or, Sub;

  assign And = RS & RT;  // AND_Gate and_1, 10 bits wide
  assign Or = RS | RT;  // OR_Gate or_1, 10 bits wide
  Adder #(.width(10)) adder_1 (.a(RS), .b(RT), .out(Add), .cin(Cin), .cout(Cout));
  Subtractor #(.width(10)) subtractor_1 (.a(RS), .b(RT), .out(Sub), .bin(Cin), .bout(Cout));
  Multiplexer #(.select(2), .width(10), .enable("false")) multiplexer_1 (
    .in0(And), .in1(Or), .in2(Add), .in3(Sub), .out(OUTPUT), .sel(Select_Opperation));

  // Other names for the same wires on the sheet: mIn[1:0] = Select_Opperation; Result[9:0] = OUTPUT; RSin[9:0] = RS;
  //   RTin[9:0] = RT
endmodule

// Format Detector
module Control (
  input  [3:0] oppcode,
  output [1:0] R_format,
  output Write_Reg_Flag,
  output Format_F,
  output [1:0] i_format,
  output L_S_flag,
  output lw_lui
);

  wire R;

  Multiplexer multiplexer_1 (.in0(1'b0), .in1(1'b1), .out(Format_F), .sel(oppcode[3]));  // open: en
  not not_1 (R, Format_F);
  Multiplexer #(.select(4)) multiplexer_2 (
    .in8(1'b0), .in10(1'b1), .out(lw_lui), .sel(oppcode));  // open: in0, in1, in2, in3, in4, in5, in6, in7, in9, in11, in12, in13, in14, in15, en
  Multiplexer #(.select(2), .width(2)) multiplexer_3 (
    .in0(2'b00), .in1(2'b01), .in2(2'b10), .in3(2'b11), .out(R_format), .sel(oppcode[1:0]), .en(R));
  Multiplexer #(.select(2), .width(2)) multiplexer_4 (
    .in0(2'b00), .in1(2'b01), .in2(2'b10), .in3(2'b11), .out(i_format), .sel(oppcode[1:0]), .en(Format_F));
  Multiplexer #(.select(4)) multiplexer_5 (
    .in0(1'b0), .in1(1'b0), .in2(1'b0), .in3(1'b0), .in4(1'b0), .in5(1'b0), .in6(1'b0), .in7(1'b0),
    .in8(1'b1), .in9(1'b0), .in10(1'b1), .in11(1'b0), .in12(1'b0), .in13(1'b0), .in14(1'b0), .in15(1'b0),
    .out(L_S_flag), .sel(oppcode));  // open: en
  Multiplexer #(.select(4)) multiplexer_6 (
    .in0(1'b1), .in1(1'b1), .in2(1'b1), .in3(1'b1), .in8(1'b1), .in9(1'b0), .in10(1'b1),
    .out(Write_Reg_Flag), .sel(oppcode));  // open: in4, in5, in6, in7, in11, in12, in13, in14, in15, en

  // Other names for the same wires on the sheet: I = Format_F; opp[1:0] = oppcode[1:0]; oppC[3:0] = oppcode;
  //   format = oppcode[3]

  // Notes on the sheet:
  //   it will check for type and will give  0 for r format, 1 for I format
endmodule

// Crtl Unit
module control_unit (
  input  [3:0] in_1,
  output Format,
  output LW,
  output SW,
  output LUI,
  output Write_Reg,
  output [1:0] ALU_Opp,
  output I,
  output R
);

  wire not_1_out, not_3_out, not_4_out, not_5_out, not_6_out, not_7_out, not_8_out;

  not not_1 (not_1_out, in_1[0]);
  not not_2 (Format, in_1[3]);
  not not_3 (not_3_out, in_1[1]);
  not not_4 (not_4_out, in_1[1]);
  not not_5 (not_5_out, in_1[2]);
  and u_LW (LW, not_1_out, not_3_out, not_5_out, in_1[3]);
  not not_6 (not_6_out, in_1[0]);
  not not_7 (not_7_out, in_1[2]);
  and u_LUI (LUI, not_6_out, in_1[1], not_8_out, in_1[3]);
  and u_SW (SW, in_1[0], not_4_out, not_7_out, in_1[3]);
  not not_8 (not_8_out, in_1[2]);
  not not_9 (I, Format);
  or or_1 (Write_Reg, Format, LW, LUI);

  assign ALU_Opp = in_1[1:0];
  assign R = Format;
endmodule
